# Fritzing sketch helloYouCircuit (saved by Fritzing 0.9.3b)
breadboards: 1

parts:
  Part1 = Adafruit Metro Mini [part_number="Adafruit #2590"]
  S1 = Pushbutton [package="[THT]"]
  R1 = Resistor [tolerance=±5% resistance=200 package=THT]

nets:
  N1: Part1.IO2, S1.Pin_3, S1.Pin_4, R1.Pin_0
  N2: Part1.+5V, S1.Pin_1, S1.Pin_2
  N3: Part1.GND, R1.Pin_1

custom parts:
  Adafruit Metro Mini: We sure love the ATmega328 here at Adafruit, and we use them a lot for our own projects. The processor has plenty of GPIO, Analog inputs, hardware UART SPI and I2C, timers and PWM galore - just enough for most simple projects. When we need to go small, we use a Pro Trinket 3V or 5V, but if you want to have USB-to-Serial built in, we reach for an Adafruit METRO Mini. METRO Mini is the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
