# Fritzing sketch forceResistor (saved by Fritzing 0.9.3b)
breadboards: 1

parts:
  Part1 = Adafruit Metro Mini [part_number="Adafruit #2590"]
  J1 = Basic Force Sensing Resistor (FSR) [package=THT]
  R1 = Resistor [tolerance=±5% resistance=27k package="2512 [SMD]"]

nets:
  N1: Part1.AD0, J1.pin_1, R1.Pin_1
  5V: Part1.+5V, J1.pin_0
  GND: Part1.GND, R1.Pin_0

custom parts:
  Adafruit Metro Mini: We sure love the ATmega328 here at Adafruit, and we use them a lot for our own projects. The processor has plenty of GPIO, Analog inputs, hardware UART SPI and I2C, timers and PWM galore - just enough for most simple projects. When we need to go small, we use a Pro Trinket 3V or 5V, but if you want to have USB-to-Serial built in, we reach for an Adafruit METRO Mini. METRO Mini is the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
